// Logisim project cpu.circ as structural Verilog: 1 circuit, main circuit main
module main (
);

  wire A_IN, A_OUT, ADDR_ABUS_OUT, ADDR_IN, ADDR_INH, ADDR_INL, ALU_C, ALU_CLC, ALU_IN, ALU_OUT, ALU_STC,
       ALU_SUB, and_1_out, and_2_out, and_3_out, and_4_out, and_5_out, and_6_out, and_7_out, and_8_out,
       and_9_out, and_11_out, B_IN, B_OUT, C, C_OUT, CLK, decoder_1_out0, decoder_1_out1, decoder_1_out2,
       decoder_1_out3, decoder_1_out4, decoder_1_out5, decoder_1_out6, decoder_1_out7, decoder_2_out0,
       decoder_2_out1, decoder_2_out2, decoder_2_out3, decoder_2_out4, decoder_2_out5, decoder_2_out6,
       decoder_2_out7, DISP_IN, FLAG_INV, HALT, HEX, IR_IN, JMP, MODE_out, nor_1_out, nor_2_out, not_1_out,
       OCTAL, or_1_out, or_2_out, or_4_out, or_5_out, OSC_out, PC_ABUS_OUT, PC_IN, PC_INC, PC_OUT, PORTA_OUT,
       PORTB_OUT, RAM_IN, RAM_OUT, RESET, ROM_OUT, RUN, RUN_STOP_out, S, S_OUT, SIGNED, STEP_out, T_RESET,
       UNSIGNED, xor_1_out, xor_2_out, xor_3_out, Z, Z_OUT;
  wire [1:0] MODE;
  wire [2:0] T_STATE;
  wire [2:2] rom_2_data;
  wire [3:0] rom_3_data_2, rom_3_data_3;
  wire [3:1] rom_2_data_2;
  wire [7:0] A_BUS, adder_1_out, controlled_buffer_5_out, controlled_buffer_12_out, IR_REG,
       multiplexer_1_out, register_1_q_2, register_4_q, register_5_q, register_6_q, register_7_q,
       register_8_q, register_9_q, register_10_q, register_11_q, register_12_q, register_13_q, register_14_q,
       register_15_q, rom_1_data, subtractor_1_out, W_BUS;
  wire [7:4] rom_3_data_4;
  wire [8:8] adder_1_cout, subtractor_1_bout;
  wire [15:0] AD_BUS, controlled_buffer_1_out, controlled_buffer_7_out, counter_1_q, counter_2_p6;
  wire [15:8] register_1_q;
  wire [23:0] rom_3_data;

  LED Df (.in(AD_BUS[15]));
  LED De (.in(AD_BUS[14]));
  LED Df_2 (.in(register_1_q[15]));
  LED De_2 (.in(register_1_q[14]));
  Register #(.width(16)) register_1 (
    .D(controlled_buffer_1_out), .en(or_1_out), .Q({register_1_q, register_1_q_2}), .clk(CLK), .clr(RESET));
  assign controlled_buffer_1_out = ADDR_INH ? {register_1_q, W_BUS} : 16'bz;  // Controlled_Buffer controlled_buffer_1
  assign controlled_buffer_1_out = ADDR_INL ? {W_BUS, register_1_q_2} : 16'bz;  // Controlled_Buffer controlled_buffer_2
  LED Dd (.in(AD_BUS[13]));
  LED Dc (.in(AD_BUS[12]));
  LED Db (.in(AD_BUS[11]));
  LED Da (.in(AD_BUS[10]));
  LED D7 (.in(W_BUS[7]));
  LED D6 (.in(W_BUS[6]));
  LED Dd_2 (.in(register_1_q[13]));
  LED Dc_2 (.in(register_1_q[12]));
  LED Db_2 (.in(register_1_q[11]));
  LED Da_2 (.in(register_1_q[10]));
  assign AD_BUS = ADDR_ABUS_OUT ? {register_1_q, register_1_q_2} : 16'bz;  // Controlled_Buffer controlled_buffer_3
  LED D9 (.in(AD_BUS[9]));
  LED D8 (.in(AD_BUS[8]));
  LED D7_2 (.in(AD_BUS[7]));
  LED D6_2 (.in(AD_BUS[6]));
  LED D5 (.in(W_BUS[5]));
  LED D4 (.in(W_BUS[4]));
  LED D3 (.in(W_BUS[3]));
  LED D2 (.in(W_BUS[2]));
  LED D9_2 (.in(register_1_q[9]));
  LED D8_2 (.in(register_1_q[8]));
  LED D7_3 (.in(register_1_q_2[7]));
  LED D6_3 (.in(register_1_q_2[6]));
  or or_1 (or_1_out, ADDR_INL, ADDR_INH);
  LED D5_2 (.in(AD_BUS[5]));
  LED D4_2 (.in(AD_BUS[4]));
  LED D3_2 (.in(AD_BUS[3]));
  LED D2_2 (.in(AD_BUS[2]));
  LED D1 (.in(W_BUS[1]));
  LED D0 (.in(W_BUS[0]));
  LED D5_3 (.in(register_1_q_2[5]));
  LED D4_3 (.in(register_1_q_2[4]));
  LED D3_3 (.in(register_1_q_2[3]));
  LED D2_3 (.in(register_1_q_2[2]));
  LED D1_2 (.in(AD_BUS[1]));
  LED D0_2 (.in(AD_BUS[0]));
  LED D1_3 (.in(register_1_q_2[1]));
  LED D0_3 (.in(register_1_q_2[0]));
  Button u_RESET (.out(RESET));
  Button RUN_STOP (.out(RUN_STOP_out));
  not not_1 (not_1_out, RAM_IN);
  assign W_BUS = RAM_OUT ? controlled_buffer_5_out : 8'bz;  // Controlled_Buffer controlled_buffer_4
  assign controlled_buffer_5_out = RAM_IN ? W_BUS : 8'bz;  // Controlled_Buffer controlled_buffer_5
  LED D7_4 (.in(counter_1_q[15]));
  LED D6_4 (.in(counter_1_q[14]));
  assign AD_BUS = PC_ABUS_OUT ? counter_1_q : 16'bz;  // Controlled_Buffer controlled_buffer_6
  Counter #(.max('hffff), .width(16)) counter_1 (
    .load(JMP), .D(AD_BUS), .count(PC_INC), .Q(counter_1_q), .clk(CLK), .clr(RESET));  // open: carry
  T_Flip_Flop #(.enable("true")) t_ff_1 (
    .clk(RUN_STOP_out), .T(1'b1), .Q(RUN), .reset(RESET), .en(1'b1));  // open: Qn, preset
  ROM #(.addrWidth(16)) rom_1 (.addr(AD_BUS), .data(rom_1_data));
  LED D7_5 (.in(counter_2_p6[15]));
  LED D6_5 (.in(counter_2_p6[14]));
  LED D5_4 (.in(counter_2_p6[13]));
  assign controlled_buffer_7_out = PC_ABUS_OUT ? counter_2_p6 : 16'bz;  // Controlled_Buffer controlled_buffer_7
  // Counter #(.max('hffff), .width(16)) counter_2: pin names not known; wires that end beside it: PC_INC, JMP, controlled_buffer_7_out, CLK, RESET, counter_2_p6
  LED D5_5 (.in(counter_1_q[13]));
  LED D4_4 (.in(counter_1_q[12]));
  LED D3_4 (.in(counter_1_q[11]));
  LED D2_4 (.in(counter_1_q[10]));
  Button STEP (.out(STEP_out));
  Clock OSC (.out(OSC_out));
  nor nor_1 (nor_1_out, C_OUT, S_OUT);
  and and_1 (and_1_out, C_OUT, xor_1_out);
  xor xor_1 (xor_1_out, C, FLAG_INV);
  and and_2 (and_2_out, Z_OUT, xor_2_out);
  xor xor_2 (xor_2_out, Z, FLAG_INV);
  and and_3 (and_3_out, S_OUT, xor_3_out);
  xor xor_3 (xor_3_out, S, FLAG_INV);
  RAM #(.addrWidth(16), .databus("bidir")) ram_1 (.addr(AD_BUS), .data(controlled_buffer_5_out));  // open: we, oe, clk
  LED D4_5 (.in(counter_2_p6[12]));
  LED D3_5 (.in(counter_2_p6[11]));
  LED D2_5 (.in(counter_2_p6[10]));
  LED D1_4 (.in(counter_2_p6[9]));
  LED D1_5 (.in(counter_1_q[9]));
  LED D0_4 (.in(counter_1_q[8]));
  LED D7_6 (.in(counter_1_q[7]));
  and and_4 (and_4_out, STEP_out, ~RUN);  // AND_Gate
  and and_5 (and_5_out, RUN, OSC_out);
  and and_6 (and_6_out, PC_IN, nor_1_out);
  and and_7 (and_7_out, PC_IN, and_1_out);
  and and_8 (and_8_out, PC_IN, and_2_out);
  and and_9 (and_9_out, PC_IN, and_3_out);
  LED D0_5 (.in(counter_2_p6[8]));
  LED D7_7 (.in(counter_2_p6[7]));
  LED D6_6 (.in(counter_2_p6[6]));
  LED D6_7 (.in(counter_1_q[6]));
  LED D5_6 (.in(counter_1_q[5]));
  LED D4_6 (.in(counter_1_q[4]));
  LED D3_6 (.in(counter_1_q[3]));
  or or_2 (or_2_out, and_4_out, and_5_out);
  and and_10 (CLK, or_2_out, ~HALT);  // AND_Gate
  or or_3 (JMP, and_6_out, and_7_out, and_8_out, and_9_out);
  LED D5_7 (.in(counter_2_p6[5]));
  LED D4_7 (.in(counter_2_p6[4]));
  LED D3_7 (.in(counter_2_p6[3]));
  LED D2_6 (.in(counter_2_p6[2]));
  LED D0_6 (.in(counter_1_q[0]));
  LED D2_7 (.in(counter_1_q[2]));
  LED D1_6 (.in(counter_1_q[1]));
  assign W_BUS = ROM_OUT ? rom_1_data : 8'bz;  // Controlled_Buffer controlled_buffer_8
  LED D1_7 (.in(counter_2_p6[1]));
  LED D0_7 (.in(counter_2_p6[0]));
  assign W_BUS = A_OUT ? A_BUS : 8'bz;  // Controlled_Buffer controlled_buffer_9
  assign W_BUS = B_OUT ? register_4_q : 8'bz;  // Controlled_Buffer controlled_buffer_10
  Counter #(.max('h7), .width(3)) counter_3 (.Q(T_STATE), .clk(CLK), .clr(or_4_out));  // open: load, D, count, carry
  or or_4 (or_4_out, T_RESET, RESET);
  Register register_2 (.D(W_BUS), .en(IR_IN), .Q(IR_REG), .clk(CLK), .clr(RESET));
  Register register_3 (.D(W_BUS), .en(A_IN), .Q(A_BUS), .clk(CLK), .clr(RESET));
  Register register_4 (.D(W_BUS), .en(B_IN), .Q(register_4_q), .clk(CLK), .clr(RESET));
  ROM #(.addrWidth(11), .dataWidth(32)) rom_2 (
    .addr({IR_REG, T_STATE}),
    .data({rom_2_data_2, PORTA_OUT, ADDR_ABUS_OUT, rom_2_data[2], PC_ABUS_OUT, ADDR_INL, ROM_OUT, ALU_SUB, ALU_CLC, ALU_STC, FLAG_INV, S_OUT, Z_OUT, C_OUT, DISP_IN, T_RESET, ALU_IN, ALU_OUT, B_IN, B_OUT, A_IN, A_OUT, IR_IN, HALT, RAM_IN, RAM_OUT, ADDR_INH, PC_INC, PC_IN, PORTB_OUT}));
  LED T0 (.in(decoder_1_out0));
  LED T1 (.in(decoder_1_out1));
  LED T2 (.in(decoder_1_out2));
  LED T3 (.in(decoder_1_out3));
  Decoder #(.select(3)) decoder_1 (
    .out0(decoder_1_out0), .out1(decoder_1_out1), .out2(decoder_1_out2), .out3(decoder_1_out3),
    .out4(decoder_1_out4), .out5(decoder_1_out5), .out6(decoder_1_out6), .out7(decoder_1_out7), .sel(T_STATE));  // open: en
  LED D7_8 (.in(IR_REG[7]));
  LED D6_8 (.in(IR_REG[6]));
  LED D5_8 (.in(IR_REG[5]));
  LED D4_8 (.in(IR_REG[4]));
  LED D7_9 (.in(A_BUS[7]));
  LED D6_9 (.in(A_BUS[6]));
  LED D5_9 (.in(A_BUS[5]));
  LED D4_9 (.in(A_BUS[4]));
  LED D7_10 (.in(register_4_q[7]));
  LED D6_10 (.in(register_4_q[6]));
  LED D5_10 (.in(register_4_q[5]));
  LED D4_10 (.in(register_4_q[4]));
  LED T4 (.in(decoder_1_out4));
  LED T5 (.in(decoder_1_out5));
  LED T6 (.in(decoder_1_out6));
  LED T7 (.in(decoder_1_out7));
  LED D3_8 (.in(IR_REG[3]));
  LED D2_8 (.in(IR_REG[2]));
  LED D1_8 (.in(IR_REG[1]));
  LED D0_8 (.in(IR_REG[0]));
  LED D3_9 (.in(A_BUS[3]));
  LED D2_9 (.in(A_BUS[2]));
  LED D1_9 (.in(A_BUS[1]));
  LED D0_9 (.in(A_BUS[0]));
  LED D3_10 (.in(register_4_q[3]));
  LED D2_10 (.in(register_4_q[2]));
  LED D1_10 (.in(register_4_q[1]));
  LED D0_10 (.in(register_4_q[0]));
  LED led_1 (.in(CLK));
  LED led_2 (.in(PC_OUT));
  LED led_3 (.in(PC_INC));
  LED led_4 (.in(RAM_OUT));
  LED led_5 (.in(HALT));
  Pull_Resistor pull_resistor_1 (.node(W_BUS));
  Register register_5 (.D(W_BUS), .en(PORTA_OUT), .Q(register_5_q), .clk(CLK));  // open: clr
  LED led_6 (.in(RUN));
  LED led_7 (.in(PC_IN));
  LED led_8 (.in(ADDR_IN));
  LED led_9 (.in(RAM_IN));
  LED led_10 (.in(IR_IN));
  Counter #(.max('h3), .width(2)) counter_4 (.Q(MODE), .clk(MODE_out));  // open: load, D, count, carry, clr
  and and_11 (and_11_out, C, C_OUT);
  Decoder #(.select(4)) decoder_2 (
    .out0(decoder_2_out0), .out1(decoder_2_out1), .out2(decoder_2_out2), .out3(decoder_2_out3),
    .out4(decoder_2_out4), .out5(decoder_2_out5), .out6(decoder_2_out6), .out7(decoder_2_out7),
    .sel(register_5_q[3:0]), .en(PORTB_OUT));  // open: out8, out9, out10, out11, out12, out13, out14, out15
  Register register_6 (.D(W_BUS), .en(DISP_IN), .Q(register_6_q), .clk(CLK), .clr(RESET));
  Button u_MODE (.out(MODE_out));
  assign W_BUS = ALU_OUT ? register_7_q : 8'bz;  // Controlled_Buffer controlled_buffer_11
  Register register_7 (.D(controlled_buffer_12_out), .en(ALU_IN), .Q(register_7_q), .clk(CLK), .clr(RESET));
  D_Flip_Flop #(.enable("true")) d_ff_1 (
    .clk(CLK), .D(ALU_C), .Q(C), .preset(ALU_STC), .en(ALU_IN), .reset(or_5_out));  // open: Qn
  or or_5 (or_5_out, RESET, ALU_CLC);
  Adder adder_1 (.a(A_BUS), .b(W_BUS), .out(adder_1_out), .cin(and_11_out), .cout(adder_1_cout[8]));
  Subtractor subtractor_1 (.a(A_BUS), .b(W_BUS), .out(subtractor_1_out), .bin(and_11_out), .bout(subtractor_1_bout[8]));
  LED led_11 (.in(ALU_IN));
  LED led_12 (.in(C_OUT));
  LED led_13 (.in(Z_OUT));
  LED led_14 (.in(S_OUT));
  _7_Segment_Display u_7_segment_display_1 (
    .g(rom_3_data_4[7]), .f(rom_3_data_4[6]), .a(rom_3_data_4[5]), .b(rom_3_data_4[4]), .e(rom_3_data_3[3]),
    .d(rom_3_data_3[2]), .c(rom_3_data_3[1]), .dp(rom_3_data_3[0]));
  _7_Segment_Display u_7_segment_display_2 (
    .g(rom_3_data[23]), .f(rom_3_data[22]), .a(rom_3_data[21]), .b(rom_3_data[20]), .e(rom_3_data_2[3]),
    .d(rom_3_data_2[2]), .c(rom_3_data_2[1]), .dp(rom_3_data_2[0]));
  LED D7_11 (.in(register_7_q[7]));
  LED D6_11 (.in(register_7_q[6]));
  LED D5_11 (.in(register_7_q[5]));
  LED D4_11 (.in(register_7_q[4]));
  assign controlled_buffer_12_out = ALU_IN ? multiplexer_1_out : 8'bz;  // Controlled_Buffer controlled_buffer_12
  Register register_8 (.D(W_BUS), .en(decoder_2_out0), .Q(register_8_q), .clk(CLK));  // open: clr
  Register register_9 (.D(W_BUS), .en(decoder_2_out1), .Q(register_9_q), .clk(CLK));  // open: clr
  Register register_10 (.D(W_BUS), .en(decoder_2_out2), .Q(register_10_q), .clk(CLK));  // open: clr
  Register register_11 (.D(W_BUS), .en(decoder_2_out3), .Q(register_11_q), .clk(CLK));  // open: clr
  Register register_12 (.D(W_BUS), .en(decoder_2_out4), .Q(register_12_q), .clk(CLK));  // open: clr
  Register register_13 (.D(W_BUS), .en(decoder_2_out5), .Q(register_13_q), .clk(CLK));  // open: clr
  Register register_14 (.D(W_BUS), .en(decoder_2_out6), .Q(register_14_q), .clk(CLK));  // open: clr
  Register register_15 (.D(W_BUS), .en(decoder_2_out7), .Q(register_15_q), .clk(CLK));  // open: clr
  LED led_15 (.in(ALU_SUB));
  LED led_16 (.in(ALU_STC));
  LED led_17 (.in(ALU_CLC));
  LED led_18 (.in(FLAG_INV));
  _7_Segment_Display u_7_segment_display_3 (
    .g(rom_3_data[15]), .f(rom_3_data[14]), .a(rom_3_data[13]), .b(rom_3_data[12]), .e(rom_3_data[11]),
    .d(rom_3_data[10]), .c(rom_3_data[9]), .dp(rom_3_data[8]));
  LED D3_11 (.in(register_7_q[3]));
  LED D2_11 (.in(register_7_q[2]));
  LED D1_11 (.in(register_7_q[1]));
  LED D0_11 (.in(register_7_q[0]));
  Register #(.width(1)) register_16 (.D(nor_2_out), .en(ALU_IN), .Q(Z), .clk(CLK), .clr(RESET));
  Multiplexer #(.width(9)) multiplexer_1 (
    .in0({adder_1_cout[8], adder_1_out}), .in1({subtractor_1_bout[8], subtractor_1_out}),
    .out({ALU_C, multiplexer_1_out}), .sel(ALU_SUB));  // open: en
  _7_Segment_Display u_7_segment_display_4 (
    .g(rom_3_data[7]), .f(rom_3_data[6]), .a(rom_3_data[5]), .b(rom_3_data[4]), .e(rom_3_data[3]),
    .d(rom_3_data[2]), .c(rom_3_data[1]), .dp(rom_3_data[0]));
  LED u_C (.in(C));
  LED u_Z (.in(Z));
  LED u_S (.in(S));
  Register #(.width(1)) register_17 (.D(multiplexer_1_out[7]), .en(ALU_IN), .Q(S), .clk(CLK), .clr(RESET));
  nor nor_2 (nor_2_out, multiplexer_1_out[3], multiplexer_1_out[2], multiplexer_1_out[1], multiplexer_1_out[0], multiplexer_1_out[7], multiplexer_1_out[6], multiplexer_1_out[5], multiplexer_1_out[4]);
  DotMatrix #(.dotshape("circle"), .inputtype("row"), .matrixcols(8), .matrixrows(8), .persist(13)) dotmatrix_1 (
    .row0(register_8_q), .row1(register_9_q), .row2(register_10_q), .row3(register_11_q),
    .row4(register_12_q), .row5(register_13_q), .row6(register_14_q), .row7(register_15_q));
  LED led_19 (.in(A_OUT));
  LED led_20 (.in(B_OUT));
  LED led_21 (.in(ALU_OUT));
  Decoder #(.select(2)) decoder_3 (.out0(UNSIGNED), .out1(SIGNED), .out2(HEX), .out3(OCTAL), .sel(MODE));  // open: en
  LED led_22 (.in(UNSIGNED));
  LED led_23 (.in(SIGNED));
  LED led_24 (.in(HEX));
  LED led_25 (.in(OCTAL));
  LED led_26 (.in(A_IN));
  LED led_27 (.in(B_IN));
  LED led_28 (.in(DISP_IN));
  ROM #(.addrWidth(10), .dataWidth(32)) rom_3 (
    .addr({MODE, register_6_q}),
    .data({rom_3_data_4, rom_3_data_3, rom_3_data[23:20], rom_3_data_2, rom_3_data[15:0]}));

  // Notes on the sheet:
  //   ADDRESS BUS
  //   DATA BUS
  //   ADDRESS REGISTER
  //   contents of rom_1 (hex, n*v repeats v):
  //   2 0 e 2 ff f 2 1 e 2 ff f 2 2 e 2 ff f 2 3 e 2 ff f 2 4 e 2 ff f 2 5 e 2 ff f 2 6 e 2 ff f 2 7 e 2
  //   ff f 2 0 e 2 0 f 2 1 e 2 0 f 2 2 e 2 0 f 2 3 e 2 0 f 2 4 e 2 0 f 2 5 e 2 0 f 2 6 e 2 0 f 2 7 e 2 0 f
  //   c 24
  //   JUMP LOGIC
  //   ROM
  //   PROGRAM COUNTER
  //   STACK POINTER
  //   RAM
  //   INSTRUCTION DECODER ROM (3x2Kx8)
  //   contents of rom_2 (hex, n*v repeats v):
  //   2800084 40 6*4000 2800084 7*4000 2800084 2800204 6*4000 2800084 280000c 3800004 8000210 4*4000
  //   2800084 2800804 6*4000 2800084 280000c 3800004 8000810 4*4000 2800084 2400 6*4000 2800084 8100
  //   6*4000 2800084 280000c 3800004 8800200 4*4000 2800084 280000c 3800004 8800800 4*4000 2800084 9000
  //   6*4000 2800084 280000c 3800004 8001020 4*4000 2800084 280000c 3800004 8000002 4*4000 2800084 1200
  //   6*4000 2800084 10000100 6*4000 2800084 101 6*4000 1920*ffffffff
  //   T STATE
  //   INSTRUCTION REGISTER
  //   A REG
  //   B REG
  //   MICROCODE
  //   CONTROL SIGNALS
  //   DISPLAY DECODER ROM (4x1Kx8)
  //   ALU REG
  //   FLAGS
  //   DISPLAY MODE DECODER
  //   contents of rom_3 (hex, n*v repeats v):
  //   compressed eJztmE1u7LoOhOdehZdw3AQYezndUnH/S3giP/EAmQQBzuQN7qT1Y5HFKtJ0oi+d1+v8jPPj53yd
  //   8lM67XWEznitR1/5/MrZOrN+fP3MXMqP9ZNPLZeRs0hPy+Izymd6HR8/PmPmcvleP/nUchk5SwtP
  //   C79ex8crjoXx8bTwtPC08LTwtPB4HTOjmhnVzKjmq2KfuVTOlE8tz0XOImktCy2M9bMslBjy4rt4
  //   KDGUGEqM9bNmSgulhdJCi4eUFiqN0kJpobTQsrCMylZUh2VUllFZRmUZlb1KV8tl5CxS42URiRGJ
  //   sX58/cxcKmfKp5WLzEZiRGJEMo/EiMSIxIjMRyRGJEa8Kn87g5XDL12sKo9fySeHyaacgZPGZrAq
  //   L38rYfHLn/Ky62FXRNYEAyeNzWAVaVfVkcOuKGpqlJeqkhzESpw07IJVxVIVkwNefFcmXhwvXvVZ
  //   1ZODsYkXLy8TRpPqnjDKWjpymGyKehcnjc1gFbwG5SVrK98HYhGxyPebIlbipLEZrEoXkSORI5Gj
  //   rLka8EKORI6y9soOL+TIYGQwMhgZOTIYGe+t9ZtrbAar4E0uL0EsQSxBvQSxBLEEsYR2B6AHEEsQ
  //   S1AvQSxBLEEsgbpBLLH7SHeSpUtWS3WTqt0cqqNk7dYw2RQrcdKwC1bVkap2c7hYlZeq3Rwmm8o+
  //   VbWbg7EZrIJuVl7+9ja6G/1td7jd43aX231udzp63aDbDfrdoOMNet6g6w363qDzDXrfoPuN6n+J
  //   Vl4mjCaMJowmjKp2a+CkYResgoZcXqov5lBeRCzy3bOXLl//fSP++0b8n38j7j/7K8Fk+WWi3lkW
  //   TGY/+vTOQmBytZ8vrKpa96R3rHfUO9tzMWSydNuTsXeufrQ9l2J70jvWO+od4acywGTHXBlicvWj
  //   8vznTxBzTXqn9MmJeqdizsnsw5/eKc85ufpRe14xH3vSO7bPqD2rPas9qz2rPetqP9uzdczWMdvL
  //   eke9sz1bx2zoXJOxd65+tD1L27M6ZnXM6piFzjmZ/WjHrI5ZuvpRe/b27O3Zt87VK/Zk+/H27O3Z
  //   27O3Z9+esxsde9I7O+bZasxWY7YaszM4W43sftvP9vzpmD8dc3VNJuqd7fnTMWe3PfZk7J2rH7Xn
  //   0Z5Hex7tebTnsXXe72BOdsz7HcxJex7b89W1cbUaV9fz1WpcrcbValytxtVqXF0bV6uRpX3sSe/s
  //   mDPPPfE9mf3o0zvbc7o88v378+fM97GGz2DwGiabYiVO2to88v2vVXAk3jUMNh0vDyux0gKtvrxW
  //   yaqGwkvWNUw2xUqcLLxUsVbBkcK7XoNNx8vDSqwKL/OxVpmfGgov81fDZFOsxMnCy3qoVXCk8D5j
  //   sOl4eViJFXgOnoPn4Dl4Dp6D5+A5eA6eg+fgOXgOnoPn4HnhTfSc6DnRc6LnRM+JnhM9J3pO9Jzo
  //   OdFzoudEz4meEz0negp+gp/gJ/gJfoKf4Cf4CX6Cn+An+Al+gp/gJ/iJ+hT1KepT1KeoT1Gfoj5F
  //   fYr6FPUp6lPUp6hPUZ+iPkV9Gnoaehp6Gnoaehp6Gnoaehp6Gnoaehp6Gnoaehp6GnoG/AJ+Ab+A
  //   X8Av4BfwC/gF/AJ+Ab+AX8Av4BfwC/gF/AJ+Ab+AX8Av4BfwC/gF/AJ+Ab+AX8Av4Bfwi83vDd4b
  //   vDd4b/De4L3Be4P3Bu8N3hu8N3hv8N7gvcF7g/cuvIGeAz0Heg70HOg50HOg50DPgZ4DPQd6DvQc
  //   6DnQc6DnQE+nvzj9xekvTn9x+ovTX5z+4vQXp784/cXpL05/cfqL01+c/uL0lwd+D/we+D3we+D3
  //   wO+B3wO/B34P/B74PfB74PfA74HfAz/BT/AT/AQ/wU/wE/wEP8FP8BP8BD/BT/AT/AQ/3eDd4N3g
  //   3eDd4N3g3eDd4N3g3eDd4N3g3eDd4N3g3YWX37/1Xc2f9Z3NYX0da/AaJptiJU5afjfre5xD2dX3
  //   ugavYbIpVuJk2dVfCDmUXf0FUYPXMNkUK3ESO8fOsXPsHDvHzrFz7LzsJnFO4pzEOYlzEuckzkmc
  //   kzgFnsATeAJP4Ak8gSfwhJ5CT6Gn0FPoKfQUego9jTiNOI04jTiNOI04jTiz8x4//A94/vA/4PHt
  //   v77z1//1/ctd4O9u/85vt3/HD/d95w/3fce3G77z1zd8/3Cn98tbvPPbLd4/3JX98nbs/HY7dvxw
  //   H3b+cB92fLsBO399A/YPd16/vOVi4CR26Cn0FHoKPYWe0r6vwg49jTiNOI04jTiNOI047bVvutLO
  //   yZ+TPyd/Tv6c/Dn5c/Ln5M/Jn5M/J39O/pz8Oflz8ufkz8mfkz8nf07+nPw5+XPy5+TP910c+fO/
  //   93HYcSe3b+X2vRz5c/Ln5M/Jn5M/J39O/pz8Oflz8ufkz8mfkz9X3wFyCwge+XPy5+TPyZ+TPyd/
  //   Tv6c/Dn5c/Ln5M/Jn5M/J39O/pz8eeXvfzQ8BsM=
endmodule
